# Fritzing sketch sensorik (saved by Fritzing 0.8.5b)
perfboards: 1

parts:
  J2 = female pin header, 17 pins [form="♀ (female)"]
  J3 = double row female pin header, 18 pins [form="♀ (female)"]
  J4 = double row female pin header, 18 pins [form="♀ (female)"]
  J1 = shrouded pin header, 8 pins [form="♂ (shrouded male)"]
  J5 = shrouded pin header, 8 pins [form="♂ (shrouded male)"]
  J6 = shrouded pin header, 8 pins [form="♂ (shrouded male)"]
  J7 = shrouded pin header, 8 pins [form="♂ (shrouded male)"]
  J8 = shrouded pin header, 8 pins [form="♂ (shrouded male)"]
  J9 = female pin header, 3 pins [form="♀ (female)"]
  J10 = shrouded pin header, 8 pins [form="♂ (shrouded male)"]
  J11 = shrouded pin header, 8 pins [form="♂ (shrouded male)"]

nets:
  N1: J2.pin1, J1.pin3, J1.pin6, J5.pin3, J5.pin6
  N2: J2.pin2, J1.pin2, J1.pin7, J5.pin2, J5.pin7
  N3: J2.pin12, J10.pin6
  N4: J2.pin13, J10.pin7
  N5: J2.pin14, J10.pin8
  N6: J2.pin15, J10.pin1
  N7: J2.pin16, J10.pin2
  N8: J2.pin17, J10.pin3
  N9: J3.pin1, J4.pin1, J1.pin1, J1.pin8, J5.pin1, J5.pin8, J6.pin1, J6.pin8, J11.pin1, J11.pin8
  N10: J3.pin6, J9.pin3
  N11: J3.pin18, J4.pin18, J1.pin4, J1.pin5, J5.pin4, J5.pin5, J6.pin4, J6.pin5, J7.pin4, J7.pin5, J8.pin4, J8.pin5, J9.pin2
  N12: J4.pin2, J8.pin2
  N13: J4.pin3, J8.pin7
  N14: J4.pin4, J7.pin2
  N15: J4.pin10, J7.pin7
  N16: J4.pin11, J6.pin2
  N17: J4.pin12, J6.pin3, J6.pin6, J7.pin3, J7.pin6, J8.pin3, J8.pin6
  N18: J4.pin13, J6.pin7
  N19: J4.pin14, J11.pin2
  N20: J4.pin15, J11.pin3
  N21: J4.pin16, J11.pin6
  N22: J4.pin17, J11.pin7
  N23: J7.pin1, J7.pin8
  N24: J8.pin1, J8.pin8
  N25: J11.pin4, J11.pin5

notes:
  I/O
  IIC
  PWM
  US
  IR
