# Fritzing sketch signalbalken (saved by Fritzing 0.8.5b)
perfboards: 1

parts:
  D1 = LED_BARGRAPH_10 [package=led_bargaph_10]
  U1 = PCF8574 [package="DIP16 [THT]"]
  U2 = PCF8574 [package="DIP16 [THT]"]
  J1 = shrouded pin header, 8 pins [form="♂ (shrouded male)"]
  R1 = Resistor [tolerance=±5% resistance=220 package=THT]
  R2 = Resistor [tolerance=±5% resistance=220 package=THT]
  R3 = Resistor [tolerance=±5% resistance=220 package=THT]
  R4 = Resistor [tolerance=±5% resistance=220 package=THT]
  R5 = Resistor [tolerance=±5% resistance=220 package=THT]
  R6 = Resistor [tolerance=±5% resistance=220 package=THT]
  R7 = Resistor [tolerance=±5% resistance=220 package=THT]
  R8 = Resistor [tolerance=±5% resistance=220 package=THT]
  R9 = Resistor [tolerance=±5% resistance=220 package=THT]
  R10 = Resistor [tolerance=±5% resistance=220 package=THT]

nets:
  N1: D1.A_A, U1.P1
  N2: D1.B_A, U1.P0
  N3: D1.C_A, U2.P7
  N4: D1.D_A, U2.P6
  N5: D1.E_A, U2.P5
  N6: D1.F_A, U2.P4
  N7: D1.G_A, U2.P3
  N8: D1.H_A, U2.P2
  N9: D1.I_A, U2.P1
  N10: D1.J_A, U2.P0
  N11: D1.J_C, R10.Pin_0
  N12: D1.I_C, R9.Pin_0
  N13: D1.H_C, R8.Pin_0
  N14: D1.G_C, R7.Pin_0
  N15: D1.F_C, R6.Pin_0
  N16: D1.E_C, R5.Pin_0
  N17: D1.D_C, R4.Pin_0
  N18: D1.C_C, R3.Pin_0
  N19: D1.B_C, R2.Pin_0
  N20: D1.A_C, R1.Pin_0
  GND: U1.A0, U1.A1, U1.GND, U2.A0, U2.GND, J1.pin1
  N21: U1.A3, U2.A1, U2.A3, U2.VCC, J1.pin4
  N22: U1.VCC, R1.Pin_1, R2.Pin_1, R3.Pin_1, R4.Pin_1, R5.Pin_1, R6.Pin_1, R7.Pin_1, R8.Pin_1, R9.Pin_1, R10.Pin_1
  N23: U2.SCL, J1.pin3
  N24: U2.SDA, J1.pin2
